// Logisim project 8_bit_cpu.circ as structural Verilog
module main (
);

  wire and_1_out, and_2_out, button_1_out, clock_1_out, instructiondecode_1_alusig,
       instructiondecode_1_checkinput, instructiondecode_1_halt, instructiondecode_1_hlselect,
       instructiondecode_1_jump, instructiondecode_1_loadcolor, instructiondecode_1_memselect,
       instructiondecode_1_mode, instructiondecode_1_readsig, instructiondecode_1_regin,
       instructiondecode_1_rset, instructiondecode_1_screen, instructiondecode_1_writesig, not_1_out,
       or_1_out;
  wire [1:0] instructiondecode_1_alua, instructiondecode_1_alub, instructiondecode_1_gregselect,
       instructiondecode_1_opselectalu, instructiondecode_1_regwrite, pull_resistor_1_node;
  wire [2:0] alu_1_flags, register_1_q;
  wire [3:0] instructiondecode_1_color, rgb_video_1_p6;
  wire [7:0] alu_1_o, multiplexer_1_out, program_1_outbyte, ramcomp_1_dataout, registers_1_aout,
       registers_1_bout, registers_1_regout, registers_1_x, registers_1_y, undriven;
  wire [15:0] registers_1_mempoint;

  Button button_1 (.out(button_1_out));
  or or_1 (or_1_out, button_1_out, instructiondecode_1_rset);
  Joystick joystick_1 ();  // open: x, y
  Joystick joystick_2 ();  // open: x, y
  Multiplexer #(.select(2), .width(8)) multiplexer_1 (
    .in0(alu_1_o), .in1(ramcomp_1_dataout), .in2(program_1_outbyte), .in3(undriven), .out(multiplexer_1_out),
    .sel(pull_resistor_1_node));
  and and_1 (and_1_out, instructiondecode_1_jump, register_1_q[2]);
  not not_1 (not_1_out, instructiondecode_1_halt);
  Clock clock_1 (.out(clock_1_out));
  and and_2 (and_2_out, clock_1_out, not_1_out);
  registers registers_1 (
    .REGIN(instructiondecode_1_regin), .REGSELECT(instructiondecode_1_gregselect),
    .INBYTE(multiplexer_1_out), .MEMSELECT(instructiondecode_1_memselect), .RESET(or_1_out),
    .OUTSELECT(instructiondecode_1_regwrite), .CLOCK(and_2_out), .ALUA(instructiondecode_1_alua),
    .ALUB(instructiondecode_1_alub), .HLSELECT(instructiondecode_1_hlselect), .REGOUT(registers_1_regout),
    .AOUT(registers_1_aout), .BOUT(registers_1_bout), .MEMPOINT(registers_1_mempoint), .X(registers_1_x),
    .Y(registers_1_y));
  \program  program_1 (
    .INPUTBYTE(registers_1_mempoint), .CLOCK(and_2_out), .RESET(or_1_out), .JUMP(and_1_out),
    .OUTBYTE(program_1_outbyte));
  Register #(.width(3)) register_1 (
    .D(alu_1_flags), .clk(instructiondecode_1_alusig), .Q(register_1_q));  // open: en, clr
  Pull_Resistor pull_resistor_1 (.node(pull_resistor_1_node));
  assign pull_resistor_1_node = instructiondecode_1_checkinput ? ~2'b11 : 2'bz;  // Controlled_Inverter controlled_inverter_1
  assign pull_resistor_1_node = instructiondecode_1_alusig ? 2'b00 : 2'bz;  // Controlled_Buffer controlled_buffer_1
  alu alu_1 (
    .CarryIn(register_1_q[0]), .A(registers_1_aout), .B(registers_1_bout),
    .OP(instructiondecode_1_opselectalu), .O(alu_1_o), .FLAGS(alu_1_flags));
  ramcomp ramcomp_1 (
    .ADDRESS(registers_1_mempoint), .WRITE(instructiondecode_1_writesig), .READ(instructiondecode_1_readsig),
    .CLOCK(and_2_out), .DATAIN(registers_1_regout), .DATAOUT(ramcomp_1_dataout));
  instructiondecode instructiondecode_1 (
    .INBYTE(program_1_outbyte), .CLOCK(and_2_out), .RESET(or_1_out),
    .LOADCOLOR(instructiondecode_1_loadcolor), .SCREEN(instructiondecode_1_screen),
    .JUMP(instructiondecode_1_jump), .HALT(instructiondecode_1_halt), .COLOR(instructiondecode_1_color),
    .ALUB(instructiondecode_1_alub), .ALUA(instructiondecode_1_alua),
    .OPSELECTALU(instructiondecode_1_opselectalu), .ALUSIG(instructiondecode_1_alusig),
    .REGWRITE(instructiondecode_1_regwrite), .WRITESIG(instructiondecode_1_writesig),
    .READSIG(instructiondecode_1_readsig), .MODE(instructiondecode_1_mode),
    .MEMSELECT(instructiondecode_1_memselect), .HLSELECT(instructiondecode_1_hlselect),
    .GREGSELECT(instructiondecode_1_gregselect), .REGIN(instructiondecode_1_regin),
    .CHECKINPUT(instructiondecode_1_checkinput), .RSET(instructiondecode_1_rset));
  assign pull_resistor_1_node = instructiondecode_1_readsig ? 2'b01 : 2'bz;  // Controlled_Buffer controlled_buffer_2
  assign pull_resistor_1_node = instructiondecode_1_mode ? 2'b10 : 2'bz;  // Controlled_Buffer controlled_buffer_3
  // RGB_Video #(.height(256), .width(256)) rgb_video_1: pin names not known; wires that end beside it: or_1_out, and_2_out, instructiondecode_1_screen, registers_1_x, registers_1_y, rgb_video_1_p6
  Register #(.width(4)) register_2 (
    .D(instructiondecode_1_color), .en(or_1_out), .clk(instructiondecode_1_loadcolor), .Q(rgb_video_1_p6));  // open: clr
endmodule

module alu (
  input  CarryIn,
  input  [7:0] A,
  input  [7:0] B,
  input  [1:0] OP,
  output [7:0] O,
  output [2:0] FLAGS
);

  wire [7:0] adder_1_out, and_1_out, not_1_out, or_1_out;

  Adder adder_1 (.a(A), .b(B), .out(adder_1_out), .cin(CarryIn), .cout(FLAGS[0]));
  assign and_1_out = A & B;  // AND_Gate and_1, 8 bits wide
  assign or_1_out = A | B;  // OR_Gate or_1, 8 bits wide
  assign not_1_out = ~A;  // NOT_Gate not_1, 8 bits wide
  Multiplexer #(.select(2), .width(8)) multiplexer_1 (
    .in0(adder_1_out), .in1(and_1_out), .in2(or_1_out), .in3(not_1_out), .out({FLAGS[1], O[6:0]}), .sel(OP));
  and and_2 (FLAGS[2], ~O[0], ~O[1], ~O[2], ~O[3], ~O[4], ~O[5], ~O[6], ~FLAGS[1]);  // AND_Gate

  assign O[7] = FLAGS[1];
endmodule

module registers (
  input  REGIN,
  input  [1:0] REGSELECT,
  input  [7:0] INBYTE,
  input  MEMSELECT,
  input  RESET,
  input  [1:0] OUTSELECT,
  input  CLOCK,
  input  [1:0] ALUA,
  input  [1:0] ALUB,
  input  HLSELECT,
  output [7:0] REGOUT,
  output [7:0] AOUT,
  output [7:0] BOUT,
  output [15:0] MEMPOINT,
  output [7:0] X,
  output [7:0] Y
);

  wire and_1_out, and_2_out, demultiplexer_3_out0, demultiplexer_3_out1, demultiplexer_3_out2,
       demultiplexer_3_out3, not_1_out, not_2_out, not_3_out, not_4_out, not_5_out, not_6_out;
  wire [7:0] A_q, B_q, demultiplexer_1_out0, demultiplexer_1_out1, demultiplexer_2_out0, demultiplexer_2_out1;

  Demultiplexer #(.width(8)) demultiplexer_1 (
    .out0(demultiplexer_1_out0), .out1(demultiplexer_1_out1), .in(INBYTE), .sel(MEMSELECT));
  and and_1 (and_1_out, MEMSELECT, ~HLSELECT);  // AND_Gate
  and and_2 (and_2_out, MEMSELECT, HLSELECT);
  Demultiplexer #(.width(8)) demultiplexer_2 (
    .out0(demultiplexer_2_out0), .out1(demultiplexer_2_out1), .in(demultiplexer_1_out1), .sel(HLSELECT));
  Demultiplexer #(.select(2)) demultiplexer_3 (
    .out0(demultiplexer_3_out0), .out1(demultiplexer_3_out1), .out2(demultiplexer_3_out2),
    .out3(demultiplexer_3_out3), .in(REGIN), .sel(REGSELECT));
  Register A (.D(demultiplexer_1_out0), .en(demultiplexer_3_out0), .clk(not_1_out), .Q(A_q), .clr(RESET));
  not not_1 (not_1_out, CLOCK);
  Register B (.D(demultiplexer_1_out0), .en(demultiplexer_3_out1), .clk(not_2_out), .Q(B_q), .clr(RESET));
  not not_2 (not_2_out, CLOCK);
  Register C (.D(demultiplexer_1_out0), .en(demultiplexer_3_out2), .clk(not_3_out), .Q(X), .clr(RESET));
  not not_3 (not_3_out, CLOCK);
  Register D (.D(demultiplexer_1_out0), .en(demultiplexer_3_out3), .clk(not_4_out), .Q(Y), .clr(RESET));
  not not_4 (not_4_out, CLOCK);
  Register MEMH (.D(demultiplexer_2_out0), .en(and_1_out), .clk(not_5_out), .Q(MEMPOINT[7:0]), .clr(RESET));
  not not_5 (not_5_out, CLOCK);
  Register MEML (.D(demultiplexer_2_out1), .en(and_2_out), .clk(not_6_out), .Q(MEMPOINT[15:8]), .clr(RESET));
  not not_6 (not_6_out, CLOCK);
  Multiplexer #(.select(2), .width(8)) multiplexer_1 (
    .in0(A_q), .in1(B_q), .in2(X), .in3(Y), .out(REGOUT), .sel(OUTSELECT));
  Multiplexer #(.select(2), .width(8)) multiplexer_2 (.in0(A_q), .in1(B_q), .in2(X), .in3(Y), .out(AOUT), .sel(ALUA));
  Multiplexer #(.select(2), .width(8)) multiplexer_3 (.in0(A_q), .in1(B_q), .in2(X), .in3(Y), .out(BOUT), .sel(ALUB));
endmodule

module ramcomp (
  input  [15:0] ADDRESS,
  input  WRITE,
  input  READ,
  input  CLOCK,
  input  [7:0] DATAIN,
  output [7:0] DATAOUT
);

  RAM #(.addrWidth(16)) ram_1 (.addr(ADDRESS), .we(WRITE), .oe(READ), .clk(CLOCK), .din(DATAIN), .dout(DATAOUT));
endmodule

module \program  (
  input  [15:0] INPUTBYTE,
  input  CLOCK,
  input  RESET,
  input  JUMP,
  output [7:0] OUTBYTE
);

  wire [15:0] adder_1_out, InstructionPointer_q, multiplexer_1_out;

  Register #(.trigger("falling"), .width(16)) InstructionPointer (
    .D(multiplexer_1_out), .clk(CLOCK), .Q(InstructionPointer_q), .clr(RESET));  // open: en
  Multiplexer #(.width(16)) multiplexer_1 (.in0(adder_1_out), .in1(INPUTBYTE), .out(multiplexer_1_out), .sel(JUMP));
  ROM #(.addrWidth(16)) rom_1 (.addr(InstructionPointer_q), .data(OUTBYTE));
  Adder #(.width(16)) adder_1 (.a(InstructionPointer_q), .b(16'h1), .out(adder_1_out));  // open: cin, cout

  // Notes on the sheet:
  //   contents of rom_1 (hex, n*v repeats v):
  //   60 0 61 0 20 20 64 33 30 10 13046*0 64 0 10
endmodule

module instructiondecode (
  input  [7:0] INBYTE,
  input  CLOCK,
  input  RESET,
  output LOADCOLOR,
  output SCREEN,
  output JUMP,
  output HALT,
  output [3:0] COLOR,
  output [1:0] ALUB,
  output [1:0] ALUA,
  output [1:0] OPSELECTALU,
  output ALUSIG,
  output [1:0] REGWRITE,
  output WRITESIG,
  output READSIG,
  output MODE,
  output MEMSELECT,
  output HLSELECT,
  output [1:0] GREGSELECT,
  output REGIN,
  output CHECKINPUT,
  output RSET
);

  wire aluops_1_awrite, aluops_1_bwrite, decoder_1_out2, decoder_1_out3, decoder_1_out4, decoder_1_out5,
       decoder_1_out6, decoder_1_out7, decoder_1_out8, loadimm_1_awrite, loadimm_1_bwrite, loadimm_1_cwrite,
       loadimm_1_dwrite, loadimm_1_hwrite, loadimm_1_lwrite, not_1_out, or_1_out, or_2_out, or_3_out,
       or_4_out, or_5_out, or_6_out, readmem_1_aread, readmem_1_bread, readmem_1_cread, readmem_1_dread,
       readmem_1_hread, readmem_1_lread;

  aluops aluops_1 (
    .ADDOP(decoder_1_out2), .ANDOP(decoder_1_out3), .OROP(decoder_1_out4), .NOTOP(decoder_1_out5),
    .ARGS(INBYTE[3:0]), .ALUSIG(ALUSIG), .OPSELECT(OPSELECTALU), .BWRITE(aluops_1_bwrite),
    .AWRITE(aluops_1_awrite), .REG1(ALUA), .REG2(ALUB));
  not not_1 (not_1_out, MODE);
  Decoder #(.select(4)) decoder_1 (
    .out0(HALT), .out1(JUMP), .out2(decoder_1_out2), .out3(decoder_1_out3), .out4(decoder_1_out4),
    .out5(decoder_1_out5), .out6(decoder_1_out6), .out7(decoder_1_out7), .out8(decoder_1_out8),
    .out9(LOADCOLOR), .out10(CHECKINPUT), .out11(RSET), .out15(SCREEN), .sel(INBYTE[7:4]), .en(not_1_out));  // open: out12, out13, out14
  or or_1 (or_1_out, readmem_1_lread, loadimm_1_lwrite);
  loadimm loadimm_1 (
    .OP(decoder_1_out6), .ARGS(INBYTE[3:0]), .CLOCK(CLOCK), .RESET(RESET), .AWRITE(loadimm_1_awrite),
    .BWRITE(loadimm_1_bwrite), .CWRITE(loadimm_1_cwrite), .DWRITE(loadimm_1_dwrite),
    .HWRITE(loadimm_1_hwrite), .LWRITE(loadimm_1_lwrite), .MODE(MODE));
  or or_2 (or_2_out, loadimm_1_dwrite, readmem_1_dread);
  or or_3 (or_3_out, readmem_1_hread, loadimm_1_hwrite);
  writemem writemem_1 (.OP(decoder_1_out7), .ARGS(INBYTE[3:0]), .WRITESIG(WRITESIG), .REGWRITE(REGWRITE));
  or or_4 (or_4_out, loadimm_1_cwrite, readmem_1_cread);
  regdecode regdecode_1 (
    .A(or_6_out), .B(or_5_out), .C(or_4_out), .D(or_2_out), .H(or_3_out), .L(or_1_out), .REGIN(REGIN),
    .REGSELECT(GREGSELECT), .HLSELECT(HLSELECT), .MEMSELECT(MEMSELECT));
  or or_5 (or_5_out, loadimm_1_bwrite, aluops_1_bwrite, readmem_1_bread);
  or or_6 (or_6_out, CHECKINPUT, loadimm_1_awrite, aluops_1_awrite, readmem_1_aread);
  readmem readmem_1 (
    .OP(decoder_1_out8), .ARGS(INBYTE[3:0]), .AREAD(readmem_1_aread), .BREAD(readmem_1_bread),
    .READMEMSIG(READSIG), .CREAD(readmem_1_cread), .DREAD(readmem_1_dread), .HREAD(readmem_1_hread),
    .LREAD(readmem_1_lread));

  assign COLOR = INBYTE[3:0];
endmodule

module aluops (
  input  ADDOP,
  input  ANDOP,
  input  OROP,
  input  NOTOP,
  input  [3:0] ARGS,
  output ALUSIG,
  output [1:0] OPSELECT,
  output BWRITE,
  output AWRITE,
  output [1:0] REG1,
  output [1:0] REG2
);

  wire and_3_out, and_4_out, and_5_out, and_6_out, and_7_out, and_8_out, and_9_out, and_10_out, and_11_out,
       and_12_out, decoder_1_out0, decoder_1_out1, decoder_1_out2, decoder_1_out3, decoder_1_out4,
       decoder_1_out5, not_1_out, or_4_out, or_5_out, or_6_out, or_7_out;
  wire [1:0] controlled_buffer_1_out, controlled_buffer_2_out;

  and and_1 (BWRITE, ARGS[3], ALUSIG);
  not not_1 (not_1_out, ARGS[3]);
  and and_2 (AWRITE, ALUSIG, not_1_out);
  or or_1 (ALUSIG, ADDOP, ANDOP, OROP, NOTOP);
  or or_2 (OPSELECT[0], NOTOP, ANDOP);
  or or_3 (OPSELECT[1], OROP, NOTOP);
  Decoder #(.select(3)) decoder_1 (
    .out0(decoder_1_out0), .out1(decoder_1_out1), .out2(decoder_1_out2), .out3(decoder_1_out3),
    .out4(decoder_1_out4), .out5(decoder_1_out5), .sel(ARGS[2:0]));  // open: out6, out7, en
  and and_3 (and_3_out, and_5_out, and_7_out);
  assign controlled_buffer_1_out = and_3_out ? 2'b00 : 2'bz;  // Controlled_Buffer controlled_buffer_1
  assign controlled_buffer_2_out = and_3_out ? 2'b01 : 2'bz;  // Controlled_Buffer controlled_buffer_2
  and and_4 (and_4_out, and_5_out, and_8_out);
  assign controlled_buffer_1_out = and_4_out ? 2'b00 : 2'bz;  // Controlled_Buffer controlled_buffer_3
  assign controlled_buffer_2_out = and_4_out ? 2'b10 : 2'bz;  // Controlled_Buffer controlled_buffer_4
  or or_4 (or_4_out, decoder_1_out0, decoder_1_out1, decoder_1_out2);
  and and_5 (and_5_out, ALUSIG, or_4_out);
  and and_6 (and_6_out, and_5_out, and_10_out);
  assign controlled_buffer_1_out = and_6_out ? 2'b00 : 2'bz;  // Controlled_Buffer controlled_buffer_5
  assign controlled_buffer_2_out = and_6_out ? 2'b11 : 2'bz;  // Controlled_Buffer controlled_buffer_6
  or or_5 (or_5_out, decoder_1_out0, decoder_1_out3, decoder_1_out4);
  and and_7 (and_7_out, ALUSIG, or_5_out);
  or or_6 (or_6_out, decoder_1_out3, decoder_1_out1, decoder_1_out5);
  and and_8 (and_8_out, ALUSIG, or_6_out);
  and and_9 (and_9_out, and_7_out, and_8_out);
  assign controlled_buffer_1_out = and_9_out ? 2'b01 : 2'bz;  // Controlled_Buffer controlled_buffer_7
  assign controlled_buffer_2_out = and_9_out ? 2'b10 : 2'bz;  // Controlled_Buffer controlled_buffer_8
  or or_7 (or_7_out, decoder_1_out2, decoder_1_out4, decoder_1_out5);
  and and_10 (and_10_out, ALUSIG, or_7_out);
  and and_11 (and_11_out, and_8_out, and_10_out);
  and and_12 (and_12_out, and_7_out, and_10_out);
  assign controlled_buffer_1_out = and_12_out ? 2'b01 : 2'bz;  // Controlled_Buffer controlled_buffer_9
  assign controlled_buffer_2_out = and_12_out ? 2'b11 : 2'bz;  // Controlled_Buffer controlled_buffer_10
  Pull_Resistor pull_resistor_1 (.node(controlled_buffer_1_out));
  assign controlled_buffer_1_out = and_11_out ? 2'b10 : 2'bz;  // Controlled_Buffer controlled_buffer_11
  assign controlled_buffer_2_out = and_11_out ? 2'b11 : 2'bz;  // Controlled_Buffer controlled_buffer_12
  Pull_Resistor pull_resistor_2 (.node(REG1));
  Multiplexer #(.select(2), .width(2)) multiplexer_1 (
    .in0(2'b00), .in1(2'b01), .in2(2'b10), .in3(2'b11), .out(REG1), .sel(controlled_buffer_1_out));
  Pull_Resistor pull_resistor_3 (.node(REG2));
  Multiplexer #(.select(2), .width(2)) multiplexer_2 (
    .in0(2'b00), .in1(2'b01), .in2(2'b10), .in3(2'b11), .out(REG2), .sel(controlled_buffer_2_out));
  Pull_Resistor pull_resistor_4 (.node(controlled_buffer_2_out));
endmodule

module loadimm (
  input  OP,
  input  [3:0] ARGS,
  input  CLOCK,
  input  RESET,
  output AWRITE,
  output BWRITE,
  output CWRITE,
  output DWRITE,
  output HWRITE,
  output LWRITE,
  output MODE
);

  wire decoder_1_out0, decoder_1_out1, decoder_1_out2, decoder_1_out3, decoder_1_out4, decoder_1_out5,
       not_1_out, not_2_out, not_3_out, not_4_out, not_5_out, not_6_out, or_1_out, or_2_out, or_4_out,
       or_5_out, or_6_out, or_7_out;

  Decoder #(.select(3)) decoder_1 (
    .out0(decoder_1_out0), .out1(decoder_1_out1), .out2(decoder_1_out2), .out3(decoder_1_out3),
    .out4(decoder_1_out4), .out5(decoder_1_out5), .sel(ARGS[2:0]), .en(OP));  // open: out6, out7
  Register #(.trigger("falling"), .width(1)) register_1 (
    .D(not_1_out), .en(or_1_out), .clk(CLOCK), .Q(AWRITE), .clr(RESET));
  not not_1 (not_1_out, AWRITE);
  or or_1 (or_1_out, AWRITE, decoder_1_out0);
  Register #(.trigger("falling"), .width(1)) register_2 (
    .D(not_2_out), .en(or_2_out), .clk(CLOCK), .Q(BWRITE), .clr(RESET));
  not not_2 (not_2_out, BWRITE);
  or or_2 (or_2_out, BWRITE, decoder_1_out1);
  or or_3 (MODE, AWRITE, BWRITE, CWRITE, DWRITE, HWRITE, LWRITE);
  Register #(.trigger("falling"), .width(1)) register_3 (
    .D(not_3_out), .en(or_4_out), .clk(CLOCK), .Q(CWRITE), .clr(RESET));
  not not_3 (not_3_out, CWRITE);
  or or_4 (or_4_out, CWRITE, decoder_1_out2);
  Register #(.trigger("falling"), .width(1)) register_4 (
    .D(not_4_out), .en(or_5_out), .clk(CLOCK), .Q(DWRITE), .clr(RESET));
  not not_4 (not_4_out, DWRITE);
  or or_5 (or_5_out, DWRITE, decoder_1_out3);
  Register #(.trigger("falling"), .width(1)) register_5 (
    .D(not_5_out), .en(or_6_out), .clk(CLOCK), .Q(HWRITE), .clr(RESET));
  not not_5 (not_5_out, HWRITE);
  or or_6 (or_6_out, HWRITE, decoder_1_out4);
  Register #(.trigger("falling"), .width(1)) register_6 (
    .D(not_6_out), .en(or_7_out), .clk(CLOCK), .Q(LWRITE), .clr(RESET));
  not not_6 (not_6_out, LWRITE);
  or or_7 (or_7_out, LWRITE, decoder_1_out5);
endmodule

module writemem (
  input  OP,
  input  [3:0] ARGS,
  output WRITESIG,
  output [1:0] REGWRITE
);


  assign REGWRITE = ARGS[1:0];
  assign WRITESIG = OP;
endmodule

module readmem (
  input  OP,
  input  [3:0] ARGS,
  output AREAD,
  output BREAD,
  output READMEMSIG,
  output CREAD,
  output DREAD,
  output HREAD,
  output LREAD
);

  Decoder #(.select(3)) decoder_1 (
    .out0(AREAD), .out1(BREAD), .out2(CREAD), .out3(DREAD), .out4(HREAD), .out5(LREAD), .sel(ARGS[2:0]),
    .en(OP));  // open: out6, out7

  assign READMEMSIG = OP;
endmodule

module regdecode (
  input  A,
  input  B,
  input  C,
  input  D,
  input  H,
  input  L,
  output REGIN,
  output [1:0] REGSELECT,
  output HLSELECT,
  output MEMSELECT
);

  or or_1 (REGSELECT[0], B, D);
  or or_2 (MEMSELECT, H, L);
  or or_3 (REGIN, D, C, A, B);
  nor nor_1 (REGSELECT[1], A, B);

  assign HLSELECT = H;
endmodule
